# Fritzing sketch fritzing (saved by Fritzing 0.9.3b)

parts:
  IC1 = ADS1115 16-bit ADC Breakout
  AMS1 = AMS1777 5V regulator module
  YF-S201_Flow_Meter1 = YF-S201 Water Flow Meter
  YF-S201_Flow_Meter2 = YF-S201 Water Flow Meter
  U1 = LM2596 step down module
  U2 = ESP32-WROOM-32D-NodeMCU
  U3 = 4RelayModule
  U4 = 4RelayModule
  DS1 = DS18B20 1-Wire Temperature Sensor [part_number=DS18B20]
  DS2 = DS18B20 1-Wire Temperature Sensor [part_number=DS18B20]
  IC2 = PCF8575
  Composant1 = BME280
  Composant2 = BME280
  R1 = Resistor [tolerance=±5% resistance=220 package=THT]
  Power_plug1 = Power plug
  R5 = Resistor [tolerance=±5% resistance=220 package=THT]  # not connected
  R3 = Resistor [tolerance=±5% resistance=220 package=THT]
  J2 = Camdenboss CTB0158-8 [part_number=CTB0158-8 package=THT]

nets:
  GND: IC1.GND, AMS1.GND-_(input), YF-S201_Flow_Meter1.GND, YF-S201_Flow_Meter2.GND, U1.IN-, U1.OUT-, DS1.GND, DS2.GND, Power_plug1.GND
  N1: IC1.SCL, U2.G22, IC2.SCL, Composant1.SCL, Composant2.SCL
  N2: IC1.SDA, U2.G21, IC2.SDA, Composant1.SDA, Composant2.SDA
  VCC: AMS1.VIN+, YF-S201_Flow_Meter1.VCC, YF-S201_Flow_Meter2.VCC
  GND_2: AMS1.GND-_(output), U2.GND, U3.GND, U4.GND, IC2.GND, Composant1.GND, Composant2.GND
  N3: YF-S201_Flow_Meter1.SIG, U2.G32
  N4: YF-S201_Flow_Meter2.SIG, U2.G33
  N5: U1.IN+, Power_plug1.VCC
  3.3V: U2.3.3V, DS1.VDD
  N6: U2.G25, J2.pin7
  N7: U2.G27, J2.terminal_8
  N8: U2.G19, DS1.DQ, DS2.DQ, R1.Pin_0
  N9: U3.IN2, IC2.GPB1
  N10: U3.IN1, IC2.GPB0
  VCC_2: U3.VCC, U4.VCC
  N11: U3.IN3, IC2.GPB2
  N12: U3.IN4, IC2.GPB3
  N13: U4.IN2, IC2.GPB5
  N14: U4.IN1, IC2.GPB4
  N15: U4.IN3, IC2.GPB6
  N16: U4.IN4, IC2.GPB7
  VIN: IC2.VCC, Composant1.VIN, Composant2.VIN, R3.Pin_0, J2.pin6

notes:
  ESP32 + ESPHOME / HA
  12v
  5v
  3.3v
  AMS1117
  LM2596 step down
  8 relais
  ADS1115
  DS18B20
  PCF8575
  4.7K
  2x BME280
  DEBIMETRE YF-DN40
  10K

custom parts:
  ADS1115 16-bit ADC Breakout: ADS1015 12-bit I2C ADC+PGA Breakout
  AMS1777 5V regulator module: AMS1777 5V regulator module source : https://github.com/ShenTengTu/fritzing_parts/tree/master/voltage%20regulator/AMS1117_5V_regulator_module
  YF-S201 Water Flow Meter: The YF-S201 Flow Meter. The input voltage is 5V to 24V (DC).
  LM2596 step down module: LM2596 DC-DC step down power supply module 3 A.
  4RelayModule: 4 relay arduino module SONGLE SRD05VDC-SL-C
